// Logisim project alu.circ as structural Verilog: 9 circuits, main circuit main
module main (
  input  [15:0] X,
  input  [15:0] Y,
  input  [2:0] Switch,
  output Equal,
  output [15:0] Result,
  output [15:0] Result_2
);

  wire [15:0] add_result, add_result_2, and_result, and_result_2, mult_result, mult_result_2, or_result,
       or_result_2, sll_result, sll_result_2, slt_result, slt_result_2, srl_result, srl_result_2, xor_result,
       xor_result_2;

  sll sll_1 (.X(X), .Y(Y), .Result(sll_result), .Result_2(sll_result_2));  // open: Switch, Equal
  srl srl_1 (.X(X), .Y(Y), .Result(srl_result), .Result_2(srl_result_2));  // open: Switch, Equal
  add add_1 (.X(X), .Y(Y), .Result(add_result), .Result_2(add_result_2));  // open: Switch, Equal
  \and  and_1 (.X(X), .Y(Y), .Result(and_result), .Result_2(and_result_2));  // open: Switch, Equal
  Multiplexer #(.select(3), .width(16)) multiplexer_1 (
    .in0(sll_result), .in1(srl_result), .in2(add_result), .in3(and_result), .in4(or_result),
    .in5(xor_result), .in6(slt_result), .in7(mult_result), .out(Result), .sel(Switch));  // open: en
  \or  or_1 (.X(X), .Y(Y), .Result(or_result), .Result_2(or_result_2));  // open: Switch, Equal
  \xor  xor_1 (.X(X), .Y(Y), .Result(xor_result), .Result_2(xor_result_2));  // open: Switch, Equal
  slt slt_1 (.X(X), .Y(Y), .Result(slt_result), .Result_2(slt_result_2));  // open: Switch, Equal
  mult mult_1 (.X(X), .Y(Y), .Result(mult_result), .Result_2(mult_result_2));  // open: Switch, Equal
  Multiplexer #(.select(3), .width(16)) multiplexer_2 (
    .in0(sll_result_2), .in1(srl_result_2), .in2(add_result_2), .in3(and_result_2), .in4(or_result_2),
    .in5(xor_result_2), .in6(slt_result_2), .in7(mult_result_2), .out(Result_2), .sel(Switch));  // open: en

  // Other names for the same wires on the sheet: S[2:0] = Switch

  // Notes on the sheet:
  //   INPUTS to your circuit
  //   DON'T CHANGE THE LOCATIONS OF THE INPUTS AND OUTPUTS!
  //   OUTPUTS from your circuit
endmodule

module sll (
  input  [15:0] X,
  input  [15:0] Y,
  input  [2:0] Switch,
  output Equal,
  output [15:0] Result,
  output [15:0] Result_2
);

  wire comparator_1_eq;
  wire [15:0] shifter_1_out;

  Shifter #(.width(16)) shifter_1 (.in(X), .\dist (Y[3:0]), .out(shifter_1_out));
  Comparator #(.width(12)) comparator_1 (.a(Y[15:4]), .b({12{1'b0}}), .eq(comparator_1_eq));  // open: gt, lt
  Multiplexer #(.width(16)) multiplexer_1 (
    .in0({16{1'b0}}), .in1(shifter_1_out), .out(Result), .sel(comparator_1_eq));  // open: en

  assign Result_2 = {16{1'b0}};

  // Other names for the same wires on the sheet: S[2:0] = Switch

  // Notes on the sheet:
  //   INPUTS to your circuit
endmodule

module srl (
  input  [15:0] X,
  input  [15:0] Y,
  input  [2:0] Switch,
  output Equal,
  output [15:0] Result,
  output [15:0] Result_2
);

  wire comparator_1_eq;
  wire [15:0] shifter_1_out;

  Shifter #(.width(16), .shift("lr")) shifter_1 (.in(X), .\dist (Y[3:0]), .out(shifter_1_out));
  Comparator #(.width(12)) comparator_1 (.a(Y[15:4]), .b({12{1'b0}}), .eq(comparator_1_eq));  // open: gt, lt
  Multiplexer #(.width(16)) multiplexer_1 (
    .in0({16{1'b0}}), .in1(shifter_1_out), .out(Result), .sel(comparator_1_eq));  // open: en

  assign Result_2 = {16{1'b0}};

  // Other names for the same wires on the sheet: S[2:0] = Switch

  // Notes on the sheet:
  //   INPUTS to your circuit
endmodule

module add (
  input  [15:0] X,
  input  [15:0] Y,
  input  [2:0] Switch,
  output Equal,
  output [15:0] Result,
  output [15:0] Result_2
);

  Adder #(.width(16)) adder_1 (.a(X), .b(Y), .out(Result));  // open: cin, cout

  assign Result_2 = {16{1'b0}};

  // Other names for the same wires on the sheet: S[2:0] = Switch

  // Notes on the sheet:
  //   INPUTS to your circuit
endmodule

module \and  (
  input  [15:0] X,
  input  [15:0] Y,
  input  [2:0] Switch,
  output Equal,
  output [15:0] Result,
  output [15:0] Result_2
);

  assign Result = X & Y;  // AND_Gate and_1, 16 bits wide

  assign Result_2 = {16{1'b0}};

  // Other names for the same wires on the sheet: S[2:0] = Switch

  // Notes on the sheet:
  //   INPUTS to your circuit
endmodule

module \or  (
  input  [15:0] X,
  input  [15:0] Y,
  input  [2:0] Switch,
  output Equal,
  output [15:0] Result,
  output [15:0] Result_2
);

  assign Result = X | Y;  // OR_Gate or_1, 16 bits wide

  assign Result_2 = {16{1'b0}};

  // Other names for the same wires on the sheet: S[2:0] = Switch

  // Notes on the sheet:
  //   INPUTS to your circuit
endmodule

module \xor  (
  input  [15:0] X,
  input  [15:0] Y,
  input  [2:0] Switch,
  output Equal,
  output [15:0] Result,
  output [15:0] Result_2
);

  assign Result = X ^ Y;  // XOR_Gate xor_1, 16 bits wide

  assign Result_2 = {16{1'b0}};

  // Other names for the same wires on the sheet: S[2:0] = Switch

  // Notes on the sheet:
  //   INPUTS to your circuit
endmodule

module slt (
  input  [15:0] X,
  input  [15:0] Y,
  input  [2:0] Switch,
  output Equal,
  output [15:0] Result,
  output [15:0] Result_2
);

  wire comparator_1_lt;

  Comparator #(.width(16)) comparator_1 (.a(X), .b(Y), .lt(comparator_1_lt));  // open: gt, eq
  assign Result = {{15{1'b0}}, comparator_1_lt};  // Bit_Extender bit_extender_1

  assign Result_2 = {16{1'b0}};

  // Other names for the same wires on the sheet: S[2:0] = Switch

  // Notes on the sheet:
  //   INPUTS to your circuit
endmodule

module mult (
  input  [15:0] X,
  input  [15:0] Y,
  input  [2:0] Switch,
  output Equal,
  output [15:0] Result,
  output [15:0] Result_2
);

  Multiplier #(.width(16)) multiplier_1 (.a(X), .b(Y), .out(Result));  // open: cin, cout

  assign Result_2 = {16{1'b0}};

  // Other names for the same wires on the sheet: S[2:0] = Switch

  // Notes on the sheet:
  //   INPUTS to your circuit
endmodule
