// Logisim project alu.circ as structural Verilog: 9 circuits, main circuit main
module main (
  input  [15:0] X,
  input  [15:0] Y,
  input  [2:0] Switch,
  output Equal,
  output [15:0] Result,
  output [15:0] Result_2
);


  // Other names for the same wires on the sheet: S[2:0] = Switch

  // Notes on the sheet:
  //   INPUTS to your circuit
  //   DON'T CHANGE THE LOCATIONS OF THE INPUTS AND OUTPUTS!
  //   OUTPUTS from your circuit
endmodule

module sll (
  input  [15:0] X,
  input  [15:0] Y,
  input  [2:0] Switch,
  output Equal,
  output [15:0] Result,
  output [15:0] Result_2
);


  // Other names for the same wires on the sheet: S[2:0] = Switch

  // Notes on the sheet:
  //   INPUTS to your circuit
endmodule

module srl (
  input  [15:0] X,
  input  [15:0] Y,
  input  [2:0] Switch,
  output Equal,
  output [15:0] Result,
  output [15:0] Result_2
);


  // Other names for the same wires on the sheet: S[2:0] = Switch

  // Notes on the sheet:
  //   INPUTS to your circuit
endmodule

module add (
  input  [15:0] X,
  input  [15:0] Y,
  input  [2:0] Switch,
  output Equal,
  output [15:0] Result,
  output [15:0] Result_2
);


  // Other names for the same wires on the sheet: S[2:0] = Switch

  // Notes on the sheet:
  //   INPUTS to your circuit
endmodule

module \and  (
  input  [15:0] X,
  input  [15:0] Y,
  input  [2:0] Switch,
  output Equal,
  output [15:0] Result,
  output [15:0] Result_2
);


  // Other names for the same wires on the sheet: S[2:0] = Switch

  // Notes on the sheet:
  //   INPUTS to your circuit
endmodule

module \or  (
  input  [15:0] X,
  input  [15:0] Y,
  input  [2:0] Switch,
  output Equal,
  output [15:0] Result,
  output [15:0] Result_2
);


  // Other names for the same wires on the sheet: S[2:0] = Switch

  // Notes on the sheet:
  //   INPUTS to your circuit
endmodule

module \xor  (
  input  [15:0] X,
  input  [15:0] Y,
  input  [2:0] Switch,
  output Equal,
  output [15:0] Result,
  output [15:0] Result_2
);


  // Other names for the same wires on the sheet: S[2:0] = Switch

  // Notes on the sheet:
  //   INPUTS to your circuit
endmodule

module slt (
  input  [15:0] X,
  input  [15:0] Y,
  input  [2:0] Switch,
  output Equal,
  output [15:0] Result,
  output [15:0] Result_2
);


  // Other names for the same wires on the sheet: S[2:0] = Switch

  // Notes on the sheet:
  //   INPUTS to your circuit
endmodule

module mult (
  input  [15:0] X,
  input  [15:0] Y,
  input  [2:0] Switch,
  output Equal,
  output [15:0] Result,
  output [15:0] Result_2
);


  // Other names for the same wires on the sheet: S[2:0] = Switch

  // Notes on the sheet:
  //   INPUTS to your circuit
endmodule
