// Logisim project regfile.circ as structural Verilog: 1 circuit, main circuit main
module main (
  input  [2:0] Read_Register_1,
  input  [2:0] Read_Register_2,
  input  [2:0] Write_Register,
  input  in_4,
  input  [15:0] Write_Data,
  input  Write_Enable,
  input  Clock,
  output [15:0] s0_Value,
  output [15:0] s1_Value,
  output [15:0] s2_Value,
  output [15:0] ra_Value,
  output [15:0] sp_Value,
  output [15:0] Read_Data_1,
  output [15:0] Read_Data_2
);

  wire WtoA0, WtoRA, WtoS0, WtoS1, WtoS2, WtoSP, WtoV0;
  wire [15:0] to0, toA0, toSp_t, toV0;

  Register #(.width(16)) register_1 (.D(Write_Data), .en(WtoRA), .Q(ra_Value), .clk(Clock));  // open: clr
  Register #(.width(16)) register_2 (.D(Write_Data), .en(WtoS0), .Q(s0_Value), .clk(Clock));  // open: clr
  Register #(.width(16)) register_3 (.D(Write_Data), .en(WtoS1), .Q(s1_Value), .clk(Clock));  // open: clr
  Register #(.width(16)) register_4 (.D(Write_Data), .en(WtoS2), .Q(s2_Value), .clk(Clock));  // open: clr
  Register #(.width(16)) register_5 (.D({16{1'b0}}), .en(in_4), .Q(to0), .clk(Clock));  // open: clr
  Register #(.width(16)) register_6 (.D(Write_Data), .en(WtoA0), .Q(toA0), .clk(Clock));  // open: clr
  Register #(.width(16)) register_7 (.D(Write_Data), .en(WtoV0), .Q(toV0), .clk(Clock));  // open: clr
  Register #(.width(16)) register_8 (.D(Write_Data), .en(WtoSP), .Q(toSp_t), .clk(Clock));  // open: clr
  Demultiplexer #(.select(3), .disabled(0)) demultiplexer_1 (
    .out1(WtoRA), .out2(WtoS0), .out3(WtoS1), .out4(WtoS2), .out5(WtoA0), .out6(WtoV0), .out7(WtoSP),
    .in(Write_Enable), .sel(Write_Register));  // open: out0, en
  Multiplexer #(.select(3), .width(16)) multiplexer_1 (
    .in0(to0), .in1(ra_Value), .in2(s0_Value), .in3(s1_Value), .in4(s2_Value), .in5(toA0), .in6(toV0),
    .in7(sp_Value), .out(Read_Data_1), .sel(Read_Register_1));  // open: en
  Multiplexer #(.select(3), .width(16)) multiplexer_2 (
    .in0(to0), .in1(ra_Value), .in2(s0_Value), .in3(s1_Value), .in4(s2_Value), .in5(toA0), .in6(toV0),
    .in7(sp_Value), .out(Read_Data_2), .sel(Read_Register_2));  // open: en

  // Other names for the same wires on the sheet: clk = Clock; read_data1[15:0] = Read_Data_1;
  //   read_data2[15:0] = Read_Data_2; read_reg1[2:0] = Read_Register_1; read_reg2[2:0] = Read_Register_2;
  //   toRA[15:0] = ra_Value; toS0[15:0] = s0_Value; toS1[15:0] = s1_Value; toS2[15:0] = s2_Value;
  //   toSP[15:0] = sp_Value; write_en = Write_Enable; write_reg[2:0] = Write_Register

  // Notes on the sheet:
  //   INPUTS to your circuit
  //   DON'T CHANGE THE LOCATIONS OF THE INPUTS AND OUTPUTS!
  //   These are DEBUG/TEST outputs from your circuit.
  //   OUTPUTS from your circuit
endmodule
